# Fritzing sketch PT1 (saved by Fritzing 1.0.5)
breadboards: 1

parts:
  R1 = Resistor [tolerance=±5% power=0.25W resistance=220 package=THT]
  Part1 = Arduino Leonardo (Rev3b)
  LED1 = LED - 5mm [color="Red (633nm)" current=0.030A package="5 mm [THT]"]
  U1 = POT [knob_status=50% power=0.5W package=pot_mammoth]  # not connected
  J1 = Basic Servo  # not connected
  LCD1 = LCD screen  # not connected
  M1 = DC Motor [voltage_(max)=6V voltage_(min)=3V]  # not connected
  Teensy_3_1 = Teensy 3.1  # not connected

nets:
  N1: R1.Pin_0, Part1.5V
  N2: R1.Pin_1, LED1.anode
  N3: Part1.GND, LED1.cathode
